# Fritzing sketch buttonstrip (saved by Fritzing 0.9.3b)
stripboards: 1

parts:
  S2 = Pushbutton [package="[THT]"]
  S3 = Pushbutton [package="[THT]"]

nets:
  N1: S2.Pin_1, S2.Pin_2, S3.Pin_1, S3.Pin_2
  N2: S2.Pin_3, S2.Pin_4, S3.Pin_3, S3.Pin_4

notes:
  <-0,45-><- 0,5-><--------- 1 ------->
  buttons (in inches)
  screw (inches):
  <---------- 1,4 -----------> <--------- 1,1-------->
  strip:
  5x28
