# Fritzing sketch radio streamer (saved by Fritzing 0.9.3b)

parts:
  PVM5102A1 = PCM5102A [package="Breakout Board"]
  PVM5102A2 = PCM8403 [package="Breakout Board"]
  MCU1 = Raspberry Pi Zero

nets:
  N1: PVM5102A1.3.3_V, PVM5102A1.XMT, MCU1.pin_1, MCU1.pin_17
  N2: PVM5102A1.GND, PVM5102A1.FLT, PVM5102A1.DMP, PVM5102A1.FMT, MCU1.pin_6, MCU1.pin_39
  N3: PVM5102A1.SCL, MCU1.pin_5
  N4: PVM5102A1.BCK, MCU1.pin_12
  N5: PVM5102A1.DIN, MCU1.pin_40
  N6: PVM5102A1.LCK, MCU1.pin_35
  N7: PVM5102A1.R, PVM5102A2.Audio_in_R
  N8: PVM5102A1.G, PVM5102A2.GND
  N9: PVM5102A1.L, PVM5102A2.Audio_in_L
  N10: PVM5102A2.VCC, MCU1.pin_4

custom parts:
  PCM8403: Stereo class D amplifier
